// Logisim project main.circ as structural Verilog: 16 circuits, main circuit main
module main (
  input  S3,
  input  S2,
  input  S1,
  input  in_4,
  input  S0
);

  wire clock_1_out, decodificador_1_out_5, decodificador_1_out_6, decodificador_1_out_7,
       decodificador_1_out_8, decodificador_1_out_9, decodificador_1_out_10, decodificador_1_out_11,
       decodificador_2_out_5, decodificador_2_out_6, decodificador_2_out_7, decodificador_2_out_8,
       decodificador_2_out_9, decodificador_2_out_10, decodificador_2_out_11, detectorf_1_f;
  wire [3:0] Estado_Siguiente_out_8, EstadoActual_q0, multiplexer_1_out, multiplexer_2_out;

  Multiplexer #(.width(4)) multiplexer_1 (
    .in0({S3, S2, S1, S0}), .in1(multiplexer_2_out), .out(multiplexer_1_out), .sel(in_4));
  Clock clock_1 (.out(clock_1_out));
  estadoguardado EstadoActual (
    .D3(multiplexer_1_out[3]), .D2(multiplexer_1_out[2]), .D1(multiplexer_1_out[1]),
    .D0(multiplexer_1_out[0]), .CLK(clock_1_out), .Q3(EstadoActual_q0[3]), .Q2(EstadoActual_q0[2]),
    .Q1(EstadoActual_q0[1]), .Q0(EstadoActual_q0[0]));
  decodificador decodificador_1 (
    .A3(EstadoActual_q0[3]), .A2(EstadoActual_q0[2]), .A1(EstadoActual_q0[1]), .A0(EstadoActual_q0[0]),
    .out_9(decodificador_1_out_9), .out_5(decodificador_1_out_5), .out_10(decodificador_1_out_10),
    .out_6(decodificador_1_out_6), .out_11(decodificador_1_out_11), .out_7(decodificador_1_out_7),
    .out_8(decodificador_1_out_8));
  _7_Segment_Display u_7_segment_display_1 (
    .g(decodificador_1_out_11), .f(decodificador_1_out_10), .a(decodificador_1_out_5),
    .b(decodificador_1_out_6), .e(decodificador_1_out_9), .d(decodificador_1_out_8), .c(decodificador_1_out_7));  // open: dp
  Multiplexer #(.width(4)) multiplexer_2 (
    .in0(Estado_Siguiente_out_8), .in1(EstadoActual_q0), .out(multiplexer_2_out), .sel(detectorf_1_f));
  detectorF detectorf_1 (
    .Q3(EstadoActual_q0[3]), .Q2(EstadoActual_q0[2]), .Q1(EstadoActual_q0[1]), .Q0(EstadoActual_q0[0]),
    .F(detectorf_1_f));
  estadosig Estado_Siguiente (
    .Q3(EstadoActual_q0[3]), .Q2(EstadoActual_q0[2]), .Q1(EstadoActual_q0[1]), .Q0(EstadoActual_q0[0]),
    .out_6(Estado_Siguiente_out_8[2]), .out_7(Estado_Siguiente_out_8[1]), .out_8(Estado_Siguiente_out_8[0]),
    .out_5(Estado_Siguiente_out_8[3]));
  _7_Segment_Display u_7_segment_display_2 (
    .g(decodificador_2_out_11), .f(decodificador_2_out_10), .a(decodificador_2_out_5),
    .b(decodificador_2_out_6), .e(decodificador_2_out_9), .d(decodificador_2_out_8), .c(decodificador_2_out_7));  // open: dp
  decodificador decodificador_2 (
    .A3(Estado_Siguiente_out_8[3]), .A2(Estado_Siguiente_out_8[2]), .A1(Estado_Siguiente_out_8[1]),
    .A0(Estado_Siguiente_out_8[0]), .out_9(decodificador_2_out_9), .out_5(decodificador_2_out_5),
    .out_10(decodificador_2_out_10), .out_6(decodificador_2_out_6), .out_11(decodificador_2_out_11),
    .out_7(decodificador_2_out_7), .out_8(decodificador_2_out_8));

  // Notes on the sheet:
  //   Nodo Actual
endmodule

module decodificador (
  input  A3,
  input  A2,
  input  A1,
  input  A0,
  output out_5,
  output out_6,
  output out_7,
  output out_8,
  output out_9,
  output out_10,
  output out_11
);

  E e_1 (.A3(A3), .A2(A2), .A1(A1), .A0(A0), .out_5(out_9));
  A a_1 (.A3(A3), .A2(A2), .A1(A1), .A0(A0), .out_5(out_5));
  F f_1 (.A3(A3), .A2(A2), .A1(A1), .A0(A0), .out_5(out_10));
  B b_1 (.A3(A3), .A2(A2), .A1(A1), .A0(A0), .out_5(out_6));
  G g_1 (.A3(A3), .A2(A2), .A1(A1), .A0(A0), .out_5(out_11));
  C c_1 (.A3(A3), .A2(A2), .A1(A1), .A0(A0), .out_5(out_7));
  D d_1 (.A3(A3), .A2(A2), .A1(A1), .A0(A0), .out_5(out_8));
endmodule

module D3 (
  input  Q3,
  input  Q2,
  input  Q1,
  input  Q0,
  output out_5
);

  wire and_1_out, and_2_out, nand_1_out, not_1_out;

  not not_1 (not_1_out, Q3);
  nand nand_1 (nand_1_out, Q2, Q1);
  and and_1 (and_1_out, Q3, nand_1_out);
  and and_2 (and_2_out, not_1_out, Q1, Q0);
  or or_1 (out_5, and_1_out, and_2_out);
endmodule

module D2 (
  input  Q3,
  input  Q2,
  input  Q1,
  input  Q0,
  output out_5
);

  wire and_1_out, and_2_out, and_3_out, and_4_out, and_5_out;

  and and_1 (and_1_out, Q3, Q2);
  and and_2 (and_2_out, Q2, Q1);
  and and_3 (and_3_out, Q3, Q1);
  and and_4 (and_4_out, Q2, Q0);
  and and_5 (and_5_out, Q3, Q0);
  or or_1 (out_5, and_1_out, and_2_out, and_3_out, and_4_out, and_5_out);
endmodule

module D1 (
  input  Q3,
  input  Q2,
  input  Q1,
  input  Q0,
  output out_5
);

  wire and_1_out, and_2_out, and_3_out, nor_1_out, nor_2_out, nor_3_out, not_1_out, or_1_out;

  not not_1 (not_1_out, Q1);
  nor nor_1 (nor_1_out, Q3, Q0);
  and and_1 (and_1_out, not_1_out, Q3);
  nor nor_2 (nor_2_out, Q1, Q0);
  nor nor_3 (nor_3_out, Q3, Q1, Q2);
  or or_1 (or_1_out, nor_1_out, and_1_out, nor_2_out);
  and and_2 (and_2_out, or_1_out, Q2);
  and and_3 (and_3_out, nor_3_out, Q0);
  or or_2 (out_5, and_2_out, and_3_out);
endmodule

module D0 (
  input  Q3,
  input  Q2,
  input  Q1,
  input  Q0,
  output out_5
);

  wire and_1_out, and_2_out, nor_1_out, not_1_out, not_2_out, xnor_1_out;

  not not_1 (not_1_out, Q0);
  not not_2 (not_2_out, Q1);
  xnor xnor_1 (xnor_1_out, Q3, Q1);
  nor nor_1 (nor_1_out, Q2, Q1, Q0);
  and and_1 (and_1_out, not_1_out, Q1);
  and and_2 (and_2_out, Q2, not_2_out, Q0);
  or or_1 (out_5, xnor_1_out, nor_1_out, and_1_out, and_2_out);
endmodule

module estadosig (
  input  Q3,
  input  Q2,
  input  Q1,
  input  Q0,
  output out_5,
  output out_6,
  output out_7,
  output out_8
);

  D3 d3_1 (.Q2(Q2), .Q1(Q1), .Q0(Q0), .Q3(Q3), .out_5(out_5));
  D2 d2_1 (.Q2(Q2), .Q1(Q1), .Q0(Q0), .Q3(Q3), .out_5(out_6));
  D1 d1_1 (.Q3(Q3), .Q2(Q2), .Q1(Q1), .Q0(Q0), .out_5(out_7));
  D0 d0_1 (.Q2(Q2), .Q1(Q1), .Q0(Q0), .Q3(Q3), .out_5(out_8));
endmodule

module estadoguardado (
  input  CLK,
  input  D3,
  input  D2,
  input  D1,
  input  D0,
  output Q3,
  output Q2,
  output Q1,
  output Q0
);

  D_Flip_Flop d_ff_1 (.D(D3), .clk(CLK), .Q(Q3));  // open: Qn, preset, reset
  D_Flip_Flop d_ff_2 (.D(D2), .clk(CLK), .Q(Q2));  // open: Qn, preset, reset
  D_Flip_Flop d_ff_3 (.D(D1), .clk(CLK), .Q(Q1));  // open: Qn, preset, reset
  D_Flip_Flop d_ff_4 (.D(D0), .clk(CLK), .Q(Q0));  // open: Qn, preset, reset
endmodule

module detectorF (
  input  Q3,
  input  Q2,
  input  Q1,
  input  Q0,
  output F
);

  wire not_1_out, not_2_out;

  not not_1 (not_1_out, Q3);
  not not_2 (not_2_out, Q1);
  and and_1 (F, not_1_out, Q2, not_2_out, Q0);
endmodule

module A (
  input  A3,
  input  A2,
  input  A1,
  input  A0,
  output out_5
);

  wire and_1_out, and_2_out, nor_1_out, not_1_out, or_1_out, or_2_out;

  or or_1 (or_1_out, A3, A2);
  not not_1 (not_1_out, A3);
  or or_2 (or_2_out, not_1_out, A2);
  nor nor_1 (nor_1_out, A3, A2, A0);
  and and_1 (and_1_out, or_1_out, A0);
  and and_2 (and_2_out, A1, or_2_out);
  or or_3 (out_5, nor_1_out, and_1_out, and_2_out);
endmodule

module B (
  input  A3,
  input  A2,
  input  A1,
  input  A0,
  output out_5
);

  wire and_1_out, and_2_out, and_3_out, nor_1_out, not_1_out, not_2_out, not_3_out, or_1_out;

  not not_1 (not_1_out, A1);
  not not_2 (not_2_out, A2);
  nor nor_1 (nor_1_out, A3, A1);
  and and_1 (and_1_out, nor_1_out, A2);
  or or_1 (or_1_out, A2, not_1_out);
  and and_2 (and_2_out, or_1_out, not_3_out);
  not not_3 (not_3_out, A0);
  and and_3 (and_3_out, A0, not_2_out, A3);
  or or_2 (out_5, and_1_out, and_2_out, and_3_out);
endmodule

module C (
  input  A3,
  input  A2,
  input  A1,
  input  A0,
  output out_5
);

  wire and_1_out, and_2_out, and_3_out, nor_1_out, not_1_out, not_2_out;

  nor nor_1 (nor_1_out, A3, A2);
  not not_1 (not_1_out, A0);
  and and_1 (and_1_out, nor_1_out, A0);
  not not_2 (not_2_out, A1);
  and and_2 (and_2_out, A1, not_1_out);
  and and_3 (and_3_out, A3, not_2_out);
  or or_1 (out_5, and_1_out, and_3_out, and_2_out);
endmodule

module D (
  input  A3,
  input  A2,
  input  A1,
  input  A0,
  output out_5
);

  wire and_1_out, and_2_out, and_3_out, and_4_out, and_5_out, not_1_out, not_2_out, not_3_out, not_4_out,
       or_1_out, or_2_out;

  not not_1 (not_1_out, A3);
  not not_2 (not_2_out, A2);
  not not_3 (not_3_out, A1);
  not not_4 (not_4_out, A0);
  or or_1 (or_1_out, A3, not_2_out, not_4_out);
  and and_1 (and_1_out, A3, not_4_out);
  and and_2 (and_2_out, not_1_out, not_3_out, A0);
  or or_2 (or_2_out, and_1_out, and_2_out);
  and and_3 (and_3_out, or_1_out, A1);
  and and_4 (and_4_out, A2, or_2_out);
  and and_5 (and_5_out, not_1_out, not_2_out, not_4_out);
  or or_3 (out_5, and_3_out, and_4_out, and_5_out);
endmodule

module E (
  input  A3,
  input  A2,
  input  A1,
  input  A0,
  output out_5
);

  wire and_1_out, and_2_out, and_3_out, and_4_out, and_5_out, not_1_out, not_2_out, not_3_out, not_4_out,
       or_1_out, or_2_out;

  not not_1 (not_1_out, A3);
  not not_2 (not_2_out, A2);
  not not_3 (not_3_out, A1);
  not not_4 (not_4_out, A0);
  and and_1 (and_1_out, A2, A1);
  and and_2 (and_2_out, not_3_out, not_4_out);
  or or_1 (or_1_out, not_2_out, A0);
  or or_2 (or_2_out, and_1_out, and_2_out);
  and and_3 (and_3_out, A3, or_1_out);
  and and_4 (and_4_out, not_1_out, or_2_out);
  and and_5 (and_5_out, A1, A0);
  or or_3 (out_5, and_3_out, and_4_out, and_5_out);
endmodule

module F (
  input  A3,
  input  A2,
  input  A1,
  input  A0,
  output out_5
);

  wire xor_1_out, xor_2_out;

  xor xor_1 (xor_1_out, A3, A0);
  xor xor_2 (xor_2_out, A2, A1);
  or or_1 (out_5, xor_1_out, xor_2_out);
endmodule

module G (
  input  A3,
  input  A2,
  input  A1,
  input  A0,
  output out_5
);

  wire and_1_out, and_2_out, nor_1_out, nor_2_out, not_1_out, or_1_out;

  nor nor_1 (nor_1_out, A3, A1);
  nor nor_2 (nor_2_out, A2, A0);
  and and_1 (and_1_out, nor_1_out, A2);
  not not_1 (not_1_out, A2);
  or or_1 (or_1_out, not_1_out, A1, A0);
  and and_2 (and_2_out, A3, or_1_out);
  or or_2 (out_5, and_1_out, and_2_out, nor_2_out);
endmodule
